// Logisim project 10324289.circ as structural Verilog: 1 circuit, main circuit Question3
// Evan O'Keeffe
module Question3 (
  input  A,
  input  B,
  input  C
);

  wire and_1_out, undriven, undriven_2, undriven_3, xor_1_out;

  xor xor_1 (xor_1_out, undriven, undriven_2);
  buf and_1 (and_1_out, undriven_3);  // AND_Gate
  LED led_1 (.in(and_1_out));

  // Notes on the sheet:
  //   D
endmodule
