// Logisim project A1-3QA.circ as structural Verilog: 1 circuit, main circuit main
module main (
  input  A,
  input  B,
  input  C
);

  wire or_1_out, undriven, undriven_2;

  LED led_1 (.in(or_1_out));
  or or_1 (or_1_out, undriven, B, undriven_2);

  // Notes on the sheet:
  //   A
endmodule
