// Logisim project A1-3QB.circ as structural Verilog: 1 circuit, main circuit main
module main (
  input  A,
  input  B,
  input  C
);

  wire and_1_out, or_1_out, undriven, undriven_2, undriven_3;

  and and_1 (and_1_out, undriven, undriven_2);
  LED led_1 (.in(or_1_out));
  or or_1 (or_1_out, and_1_out, undriven_3);

  // Notes on the sheet:
  //   B
endmodule
