// Logisim project A1-3QC.circ as structural Verilog: 1 circuit, main circuit main
module main (
  input  A,
  input  B,
  input  C
);

  wire and_1_out, not_1_out, or_1_out, undriven, undriven_2, undriven_3;

  or or_1 (or_1_out, undriven, undriven_2);
  and and_1 (and_1_out, or_1_out, undriven_3);
  not not_1 (not_1_out, and_1_out);
  LED led_1 (.in(not_1_out));

  // Notes on the sheet:
  //   C
endmodule
