// Logisim project As3_1Min.circ as structural Verilog: 1 circuit, main circuit main
module main (
  input  A,
  input  B,
  input  C,
  input  D
);

  wire A_nBD_out, AC_out, B_nD_out, BC_out, not_1_out, not_2_out, or_1_out;

  not not_1 (not_1_out, B);
  and A_nBD (A_nBD_out, A, not_1_out, D);
  and AC (AC_out, A, C);
  and BC (BC_out, B, C);
  or or_1 (or_1_out, A_nBD_out, AC_out, BC_out, B_nD_out);
  LED led_1 (.in(or_1_out));
  not not_2 (not_2_out, D);
  and B_nD (B_nD_out, B, not_2_out);

  // Notes on the sheet:
  //   MSB
  //   LSB
endmodule
