// Logisim project As3_2MIN.circ as structural Verilog: 1 circuit, main circuit main
module main (
  input  A,
  input  B,
  input  C,
  input  D
);

  wire nA_nB_out, nA_nC_nD_out, nB_nC_out, not_1_out, not_2_out, not_3_out, not_4_out, not_5_out, not_6_out,
       not_7_out, or_1_out;

  not not_1 (not_1_out, A);
  not not_2 (not_2_out, B);
  and nA_nB (nA_nB_out, not_1_out, not_2_out);
  not not_3 (not_3_out, B);
  not not_4 (not_4_out, C);
  and nB_nC (nB_nC_out, not_3_out, not_4_out);
  or or_1 (or_1_out, nA_nB_out, nB_nC_out, nA_nC_nD_out);
  LED led_1 (.in(or_1_out));
  not not_5 (not_5_out, A);
  not not_6 (not_6_out, C);
  and nA_nC_nD (nA_nC_nD_out, not_5_out, not_6_out, not_7_out);
  not not_7 (not_7_out, D);

  // Notes on the sheet:
  //   MSB
  //   LSB
endmodule
