// Logisim project 2ComplementFullAdder.circ as structural Verilog: 4 circuits, main circuit 2CFA
module _8bit_2_s_Complement_Adder (
  input  Set,
  input  Carry_in,
  input  in_3,
  input  in_4,
  input  in_5,
  input  in_6,
  input  in_7,
  input  in_8,
  input  in_9,
  input  in_10,
  input  in_11,
  input  in_12,
  input  in_13,
  input  in_14,
  input  in_15,
  input  in_16,
  input  in_17,
  input  in_18,
  output out_19,
  output out_20,
  output out_21,
  output out_22,
  output out_23,
  output out_24,
  output out_25,
  output out_26,
  output out_27
);

  wire n2cfa_1_carry_out, n2cfa_2_carry_out, n2cfa_3_carry_out, n2cfa_4_carry_out, n2cfa_5_carry_out,
       n2cfa_6_carry_out, n2cfa_7_carry_out;

  _2CFA u_2cfa_1 (
    .B(in_4), .Set(Set), .A(in_3), .Sum_N_out(out_19), .Carry_in(Carry_in), .Carry_out(n2cfa_1_carry_out));
  _2CFA u_2cfa_2 (
    .B(in_6), .Set(Set), .A(in_5), .Sum_N_out(out_20), .Carry_in(n2cfa_1_carry_out),
    .Carry_out(n2cfa_2_carry_out));
  _2CFA u_2cfa_3 (
    .B(in_8), .Set(Set), .A(in_7), .Sum_N_out(out_21), .Carry_in(n2cfa_2_carry_out),
    .Carry_out(n2cfa_3_carry_out));
  _2CFA u_2cfa_4 (
    .B(in_10), .Set(Set), .A(in_9), .Sum_N_out(out_22), .Carry_in(n2cfa_3_carry_out),
    .Carry_out(n2cfa_4_carry_out));
  _2CFA u_2cfa_5 (
    .B(in_12), .Set(Set), .A(in_11), .Sum_N_out(out_23), .Carry_in(n2cfa_4_carry_out),
    .Carry_out(n2cfa_5_carry_out));
  _2CFA u_2cfa_6 (
    .B(in_14), .Set(Set), .A(in_13), .Sum_N_out(out_24), .Carry_in(n2cfa_5_carry_out),
    .Carry_out(n2cfa_6_carry_out));
  _2CFA u_2cfa_7 (
    .B(in_16), .Set(Set), .A(in_15), .Sum_N_out(out_25), .Carry_in(n2cfa_6_carry_out),
    .Carry_out(n2cfa_7_carry_out));
  _2CFA u_2cfa_8 (
    .B(in_18), .Set(Set), .A(in_17), .Sum_N_out(out_26), .Carry_in(n2cfa_7_carry_out), .Carry_out(out_27));
endmodule

module _2CFA (
  input  A,
  input  B,
  input  Set,
  input  Carry_in,
  output Sum_N_out,
  output Carry_out
);

  wire and_1_out, and_2_out, xor_1_out, xor_2_out;

  xor xor_1 (xor_1_out, B, Set);
  xor xor_2 (xor_2_out, A, xor_1_out);
  and and_1 (and_1_out, xor_2_out, Carry_in);
  and and_2 (and_2_out, A, xor_1_out);
  xor xor_3 (Sum_N_out, xor_2_out, Carry_in);
  or or_1 (Carry_out, and_1_out, and_2_out);
endmodule

module _2ComplementNegation (
  input  in_1,
  input  in_2,
  input  in_3,
  input  in_4,
  input  in_5,
  input  in_6,
  input  in_7,
  input  in_8,
  input  in_9,
  input  in_10,
  input  in_11,
  input  in_12,
  input  in_13,
  input  in_14,
  input  in_15,
  input  in_16,
  input  in_17,
  output out_18,
  output out_19,
  output out_20,
  output out_21,
  output out_22,
  output out_23,
  output out_24,
  output out_25,
  output out_26
);

  wire not_1_out, not_2_out, not_3_out, not_4_out, not_5_out, not_6_out, not_7_out, not_8_out;

  not not_1 (not_1_out, in_1);
  not not_2 (not_2_out, in_5);
  not not_3 (not_3_out, in_4);
  not not_4 (not_4_out, in_3);
  not not_5 (not_5_out, in_2);
  not not_6 (not_6_out, in_8);
  not not_7 (not_7_out, in_7);
  not not_8 (not_8_out, in_6);
  _8bit_2_s_Complement_Adder u_8bit_2_s_complement_adder_1 (
    .in_3(not_6_out), .in_4(in_17), .in_5(not_7_out), .in_6(in_16), .in_7(not_8_out), .in_8(in_15),
    .in_9(not_2_out), .in_10(in_14), .in_11(not_3_out), .in_12(in_13), .in_13(not_4_out), .in_14(in_12),
    .in_15(not_5_out), .in_16(in_11), .in_17(not_1_out), .in_18(in_10), .out_19(out_18), .out_20(out_19),
    .out_21(out_20), .out_22(out_21), .out_23(out_22), .out_24(out_23), .out_25(out_24), .out_26(out_25),
    .Set(in_9), .Carry_in(in_9), .out_27(out_26));
endmodule

module Main (
  input  Number_A,
  input  in_2,
  input  in_3,
  input  in_4,
  input  in_5,
  input  in_6,
  input  in_7,
  input  in_8,
  input  Set,
  input  Add_1,
  input  in_11,
  input  in_12,
  input  in_13,
  input  in_14,
  input  in_15,
  input  in_16,
  input  in_17
);

  wire _8bit_2C_Negator_out_18, _8bit_2C_Negator_out_19, _8bit_2C_Negator_out_20, _8bit_2C_Negator_out_21,
       _8bit_2C_Negator_out_22, _8bit_2C_Negator_out_23, _8bit_2C_Negator_out_24, _8bit_2C_Negator_out_25,
       _8bit_2C_Negator_out_26;

  _2ComplementNegation _8bit_2C_Negator (
    .in_1(Number_A), .in_2(in_2), .in_3(in_3), .in_4(in_4), .in_5(in_5), .in_6(in_6), .in_7(in_7),
    .in_8(in_8), .in_9(Set), .in_10(Add_1), .in_11(in_11), .in_12(in_12), .in_13(in_13), .in_14(in_14),
    .in_15(in_15), .in_16(in_16), .in_17(in_17), .out_26(_8bit_2C_Negator_out_26),
    .out_18(_8bit_2C_Negator_out_18), .out_19(_8bit_2C_Negator_out_19), .out_20(_8bit_2C_Negator_out_20),
    .out_21(_8bit_2C_Negator_out_21), .out_22(_8bit_2C_Negator_out_22), .out_23(_8bit_2C_Negator_out_23),
    .out_24(_8bit_2C_Negator_out_24), .out_25(_8bit_2C_Negator_out_25));
  LED Carry_out (.in(_8bit_2C_Negator_out_26));
  LED led_1 (.in(_8bit_2C_Negator_out_24));
  LED led_2 (.in(_8bit_2C_Negator_out_23));
  LED led_3 (.in(_8bit_2C_Negator_out_25));
  LED led_4 (.in(_8bit_2C_Negator_out_22));
  LED led_5 (.in(_8bit_2C_Negator_out_21));
  LED led_6 (.in(_8bit_2C_Negator_out_19));
  LED led_7 (.in(_8bit_2C_Negator_out_20));
  LED led_8 (.in(_8bit_2C_Negator_out_18));

  // Notes on the sheet:
  //   The negation is done by first negating each element and then adding 1 to it
  //   Set = 0 for this
endmodule
