// Logisim project 2ComplementhalfAdder.circ as structural Verilog: 1 circuit, main circuit main
module main (
  input  in_1,
  input  in_2,
  input  in_3,
  output out_4,
  output out_5
);

  wire xor_1_out;

  xor xor_1 (xor_1_out, in_2, in_3);
  xor xor_2 (out_4, in_1, xor_1_out);
  and and_1 (out_5, in_1, xor_1_out);

  // Notes on the sheet:
  //   carry 1
  //   S1
endmodule
