// Logisim project Assignment4-1.circ as structural Verilog: 3 circuits, main circuit main
module main (
  input  in_1,
  input  in_2,
  input  in_3,
  input  in_4,
  input  in_5,
  input  in_6,
  input  in_7,
  input  in_8,
  input  in_9,
  input  in_10,
  input  in_11,
  input  in_12,
  input  in_13,
  input  in_14,
  input  in_15,
  input  in_16
);

  wire fulladder_1_out_4, fulladder_1_out_5, fulladder_2_out_4, fulladder_2_out_5, fulladder_3_out_4,
       fulladder_3_out_5, fulladder_4_out_4, fulladder_4_out_5, fulladder_5_out_4, fulladder_5_out_5,
       fulladder_6_out_4, fulladder_6_out_5, fulladder_7_out_4, fulladder_7_out_5, halfadder_1_out_3,
       halfadder_1_out_4;

  LED led_1 (.in(fulladder_7_out_5));
  HalfAdder halfadder_1 (.in_1(in_1), .in_2(in_2), .out_3(halfadder_1_out_3), .out_4(halfadder_1_out_4));
  FullAdder fulladder_1 (
    .in_1(in_3), .in_2(in_4), .in_3(halfadder_1_out_4), .out_5(fulladder_1_out_5), .out_4(fulladder_1_out_4));
  FullAdder fulladder_2 (
    .in_1(in_5), .in_2(in_6), .in_3(fulladder_1_out_5), .out_5(fulladder_2_out_5), .out_4(fulladder_2_out_4));
  FullAdder fulladder_3 (
    .in_1(in_7), .in_2(in_8), .in_3(fulladder_2_out_5), .out_5(fulladder_3_out_5), .out_4(fulladder_3_out_4));
  FullAdder fulladder_4 (
    .in_1(in_9), .in_2(in_10), .in_3(fulladder_3_out_5), .out_5(fulladder_4_out_5), .out_4(fulladder_4_out_4));
  FullAdder fulladder_5 (
    .in_1(in_11), .in_2(in_12), .in_3(fulladder_4_out_5), .out_5(fulladder_5_out_5), .out_4(fulladder_5_out_4));
  FullAdder fulladder_6 (
    .in_1(in_13), .in_2(in_14), .in_3(fulladder_5_out_5), .out_5(fulladder_6_out_5), .out_4(fulladder_6_out_4));
  FullAdder fulladder_7 (
    .in_1(in_15), .in_2(in_16), .in_3(fulladder_6_out_5), .out_5(fulladder_7_out_5), .out_4(fulladder_7_out_4));
  LED led_2 (.in(fulladder_6_out_4));
  LED led_3 (.in(fulladder_7_out_4));
  LED led_4 (.in(fulladder_4_out_4));
  LED led_5 (.in(fulladder_5_out_4));
  LED led_6 (.in(fulladder_2_out_4));
  LED led_7 (.in(fulladder_3_out_4));
  LED led_8 (.in(fulladder_1_out_4));
  LED led_9 (.in(halfadder_1_out_3));
endmodule

module FullAdder (
  input  in_1,
  input  in_2,
  input  in_3,
  output out_4,
  output out_5
);

  wire and_1_out, and_2_out, xor_1_out;

  and and_1 (and_1_out, in_1, in_2);
  xor xor_1 (xor_1_out, in_1, in_2);
  or or_1 (out_5, and_1_out, and_2_out);
  and and_2 (and_2_out, in_3, xor_1_out);
  xor xor_2 (out_4, xor_1_out, in_3);
endmodule

module HalfAdder (
  input  in_1,
  input  in_2,
  output out_3,
  output out_4
);

  xor xor_1 (out_3, in_1, in_2);
  and and_1 (out_4, in_1, in_2);

  // Notes on the sheet:
  //   carry 1
  //   S1
endmodule
