// Logisim project Assignment4-3.circ as structural Verilog: 3 circuits, main circuit 2CFA
module _8bit_2_s_Complement_Adder (
  input  Set,
  input  Carry_In,
  input  A0,
  input  B0,
  input  in_5,
  input  in_6,
  input  in_7,
  input  in_8,
  input  in_9,
  input  in_10,
  input  in_11,
  input  in_12,
  input  in_13,
  input  in_14,
  input  in_15,
  input  in_16,
  input  A7,
  input  B7,
  output out_19,
  output out_20,
  output out_21,
  output out_22,
  output out_23,
  output out_24,
  output out_25,
  output out_26,
  output out_27
);

  wire n2cfa_1_carry_out, n2cfa_2_carry_out, n2cfa_3_carry_out, n2cfa_4_carry_out, n2cfa_5_carry_out,
       n2cfa_6_carry_out, n2cfa_7_carry_out;

  _2CFA u_2cfa_1 (.B(B0), .Set(Set), .A(A0), .Sum_N_out(out_19), .Carry_in(Carry_In), .Carry_out(n2cfa_1_carry_out));
  _2CFA u_2cfa_2 (
    .B(in_6), .Set(Set), .A(in_5), .Sum_N_out(out_20), .Carry_in(n2cfa_1_carry_out),
    .Carry_out(n2cfa_2_carry_out));
  _2CFA u_2cfa_3 (
    .B(in_8), .Set(Set), .A(in_7), .Sum_N_out(out_21), .Carry_in(n2cfa_2_carry_out),
    .Carry_out(n2cfa_3_carry_out));
  _2CFA u_2cfa_4 (
    .B(in_10), .Set(Set), .A(in_9), .Sum_N_out(out_22), .Carry_in(n2cfa_3_carry_out),
    .Carry_out(n2cfa_4_carry_out));
  _2CFA u_2cfa_5 (
    .B(in_12), .Set(Set), .A(in_11), .Sum_N_out(out_23), .Carry_in(n2cfa_4_carry_out),
    .Carry_out(n2cfa_5_carry_out));
  _2CFA u_2cfa_6 (
    .B(in_14), .Set(Set), .A(in_13), .Sum_N_out(out_24), .Carry_in(n2cfa_5_carry_out),
    .Carry_out(n2cfa_6_carry_out));
  _2CFA u_2cfa_7 (
    .B(in_16), .Set(Set), .A(in_15), .Sum_N_out(out_25), .Carry_in(n2cfa_6_carry_out),
    .Carry_out(n2cfa_7_carry_out));
  _2CFA u_2cfa_8 (.B(B7), .Set(Set), .A(A7), .Sum_N_out(out_26), .Carry_in(n2cfa_7_carry_out), .Carry_out(out_27));

  // Notes on the sheet:
  //   8 bit 2 complement adder
endmodule

module _2CFA (
  input  A,
  input  B,
  input  Set,
  input  Carry_in,
  output Sum_N_out,
  output Carry_out
);

  wire and_1_out, and_2_out, xor_1_out, xor_2_out;

  xor xor_1 (xor_1_out, B, Set);
  xor xor_2 (xor_2_out, A, xor_1_out);
  and and_1 (and_1_out, xor_2_out, Carry_in);
  and and_2 (and_2_out, A, xor_1_out);
  xor xor_3 (Sum_N_out, xor_2_out, Carry_in);
  or or_1 (Carry_out, and_1_out, and_2_out);

  // Notes on the sheet:
  //   2CFA = 2's Complement Full Adder
  //   S=0 : Add | S=1:Subtract
  //   S = select the add/subtract function
endmodule

module Main (
  input  Set,
  input  B,
  input  in_3,
  input  in_4,
  input  in_5,
  input  in_6,
  input  in_7,
  input  in_8,
  input  in_9,
  input  A,
  input  in_11,
  input  in_12,
  input  in_13,
  input  in_14,
  input  in_15,
  input  in_16,
  input  in_17
);

  wire _8_Bit_2_Complement_Adder_out_19, _8_Bit_2_Complement_Adder_out_20, _8_Bit_2_Complement_Adder_out_21,
       _8_Bit_2_Complement_Adder_out_22, _8_Bit_2_Complement_Adder_out_23, _8_Bit_2_Complement_Adder_out_24,
       _8_Bit_2_Complement_Adder_out_25, _8_Bit_2_Complement_Adder_out_26, _8_Bit_2_Complement_Adder_out_27;

  LED led_1 (.in(_8_Bit_2_Complement_Adder_out_27));
  _8bit_2_s_Complement_Adder _8_Bit_2_Complement_Adder (
    .A0(in_17), .B0(in_9), .in_5(in_16), .in_6(in_8), .in_7(in_15), .in_8(in_7), .in_9(in_14), .in_10(in_6),
    .in_11(in_13), .in_12(in_5), .in_13(in_12), .in_14(in_4), .in_15(in_11), .in_16(in_3), .A7(A), .B7(B),
    .out_19(_8_Bit_2_Complement_Adder_out_19), .out_20(_8_Bit_2_Complement_Adder_out_20),
    .out_21(_8_Bit_2_Complement_Adder_out_21), .out_22(_8_Bit_2_Complement_Adder_out_22),
    .out_23(_8_Bit_2_Complement_Adder_out_23), .out_24(_8_Bit_2_Complement_Adder_out_24),
    .out_25(_8_Bit_2_Complement_Adder_out_25), .out_26(_8_Bit_2_Complement_Adder_out_26), .Set(Set),
    .Carry_In(Set), .out_27(_8_Bit_2_Complement_Adder_out_27));
  LED led_2 (.in(_8_Bit_2_Complement_Adder_out_25));
  LED led_3 (.in(_8_Bit_2_Complement_Adder_out_26));
  LED led_4 (.in(_8_Bit_2_Complement_Adder_out_24));
  LED led_5 (.in(_8_Bit_2_Complement_Adder_out_21));
  LED led_6 (.in(_8_Bit_2_Complement_Adder_out_22));
  LED led_7 (.in(_8_Bit_2_Complement_Adder_out_23));
  LED led_8 (.in(_8_Bit_2_Complement_Adder_out_19));
  LED led_9 (.in(_8_Bit_2_Complement_Adder_out_20));

  // Notes on the sheet:
  //   First Carry in is linked to the set bit
  //   MSB
  //   LSB
endmodule
