// Logisim project Assignment4-4.circ as structural Verilog: 4 circuits, main circuit 2*a
module _2_a (
  input  Set,
  input  in_2,
  input  in_3,
  input  in_4,
  input  in_5,
  input  in_6,
  input  in_7,
  input  in_8,
  input  in_9,
  output out_10,
  output out_11,
  output out_12,
  output out_13,
  output out_14,
  output out_15,
  output out_16,
  output out_17,
  output Cout
);

  _8bit_2_s_Complement_Adder u_8bit_2_s_complement_adder_1 (
    .in_3(in_2), .in_4(in_2), .in_5(in_3), .in_6(in_3), .in_7(in_4), .in_8(in_4), .in_9(in_5), .in_10(in_5),
    .in_11(in_6), .in_12(in_6), .in_13(in_7), .in_14(in_7), .in_15(in_8), .in_16(in_8), .in_17(in_9),
    .in_18(in_9), .out_19(out_10), .out_20(out_11), .out_21(out_12), .out_22(out_13), .out_23(out_14),
    .out_24(out_15), .out_25(out_16), .out_26(out_17), .Set(Set), .Carry_in(Set), .out_27(Cout));
endmodule

module HalfAdder (
  input  A,
  input  B,
  output S,
  output Cout
);

  xor xor_1 (S, A, B);
  and and_1 (Cout, A, B);
endmodule

module FullAdder (
  input  A,
  input  B,
  input  Cin,
  output S,
  output Cout
);

  wire and_1_out, and_2_out, xor_1_out;

  xor xor_1 (xor_1_out, A, B);
  and and_1 (and_1_out, xor_1_out, Cin);
  and and_2 (and_2_out, A, B);
  xor xor_2 (S, xor_1_out, Cin);
  or or_1 (Cout, and_1_out, and_2_out);
endmodule

module _2_a_b (
  input  in_1,
  input  B,
  input  in_3,
  input  in_4,
  input  in_5,
  input  in_6,
  input  in_7,
  input  in_8,
  input  in_9,
  input  in_10,
  input  Add_1,
  input  in_12,
  input  in_13,
  input  in_14,
  input  in_15,
  input  minus_B,
  input  Set_0_for_Add,
  input  in_18,
  input  in_19,
  input  in_20,
  input  A,
  input  in_22,
  input  in_23,
  input  in_24,
  input  in_25,
  input  Set_0_for_Add_2,
  output out_27,
  output out_28,
  output out_29,
  output out_30,
  output out_31,
  output out_32,
  output out_33,
  output out_34,
  output out_35,
  output out_36
);

  wire n2_a_1_cout, n2_a_1_out_10, n2_a_1_out_11, n2_a_1_out_12, n2_a_1_out_13, n2_a_1_out_14, n2_a_1_out_15,
       n2_a_1_out_16, n2_a_1_out_17, n2complementnegation_1_out_18, n2complementnegation_1_out_19,
       n2complementnegation_1_out_20, n2complementnegation_1_out_21, n2complementnegation_1_out_22,
       n2complementnegation_1_out_23, n2complementnegation_1_out_24, n2complementnegation_1_out_25;

  _2_a u_2_a_1 (
    .Set(Set_0_for_Add), .out_10(n2_a_1_out_10), .out_11(n2_a_1_out_11), .out_12(n2_a_1_out_12),
    .out_13(n2_a_1_out_13), .out_14(n2_a_1_out_14), .out_15(n2_a_1_out_15), .out_16(n2_a_1_out_16),
    .out_17(n2_a_1_out_17), .in_9(in_18), .in_8(in_19), .in_7(in_20), .in_6(A), .in_2(in_25), .in_3(in_24),
    .in_4(in_23), .in_5(in_22), .Cout(n2_a_1_cout));
  _8bit_2_s_Complement_Adder u_8bit_2_s_complement_adder_1 (
    .in_3(n2_a_1_out_10), .in_4(n2complementnegation_1_out_18), .in_5(n2_a_1_out_11),
    .in_6(n2complementnegation_1_out_19), .in_7(n2_a_1_out_12), .in_8(n2complementnegation_1_out_20),
    .in_9(n2_a_1_out_13), .in_10(n2complementnegation_1_out_21), .in_11(n2_a_1_out_14),
    .in_12(n2complementnegation_1_out_22), .in_13(n2_a_1_out_15), .in_14(n2complementnegation_1_out_23),
    .in_15(n2_a_1_out_16), .in_16(n2complementnegation_1_out_24), .in_17(n2_a_1_out_17),
    .in_18(n2complementnegation_1_out_25), .out_19(out_36), .out_20(out_35), .out_21(out_34),
    .out_22(out_33), .out_23(out_32), .out_24(out_31), .out_25(out_30), .out_26(out_29),
    .Set(Set_0_for_Add_2), .Carry_in(n2_a_1_cout), .out_27(out_28));
  _2ComplementNegation u_2complementnegation_1 (
    .in_1(in_1), .in_2(B), .in_3(in_3), .in_4(in_4), .in_5(in_5), .in_6(in_6), .in_7(in_7), .in_8(in_8),
    .in_9(Set_0_for_Add_2), .in_10(in_9), .in_11(in_10), .in_12(Add_1), .in_13(in_12), .in_14(in_13),
    .in_15(in_14), .in_16(in_15), .in_17(minus_B), .out_26(out_27), .out_18(n2complementnegation_1_out_18),
    .out_19(n2complementnegation_1_out_19), .out_20(n2complementnegation_1_out_20),
    .out_21(n2complementnegation_1_out_21), .out_22(n2complementnegation_1_out_22),
    .out_23(n2complementnegation_1_out_23), .out_24(n2complementnegation_1_out_24),
    .out_25(n2complementnegation_1_out_25));

  // Notes on the sheet:
  //   2A
  //   2*a-b
endmodule
