// Logisim project As2_1.circ as structural Verilog: 1 circuit, main circuit main
module main (
  input  A_LSB,
  input  B,
  input  C,
  input  D_MSB
);

  wire A_nBCD_out, AB_nCD_out, AB_nD_out, AC_nD_out, nAB_nC_nD_out, not_1_out, not_2_out, not_3_out,
       not_4_out, or_1_out;

  not not_1 (not_1_out, A_LSB);
  not not_2 (not_2_out, B);
  not not_3 (not_3_out, C);
  not not_4 (not_4_out, D_MSB);
  and AB_nD (AB_nD_out, A_LSB, B, not_4_out);
  and nAB_nC_nD (nAB_nC_nD_out, not_1_out, B, not_3_out, not_4_out);
  and A_nBCD (A_nBCD_out, A_LSB, not_2_out, C, D_MSB);
  and AB_nCD (AB_nCD_out, A_LSB, B, not_3_out, D_MSB);
  and AC_nD (AC_nD_out, A_LSB, C, not_4_out);
  or or_1 (or_1_out, AB_nD_out, nAB_nC_nD_out, A_nBCD_out, AB_nCD_out, AC_nD_out);
  LED led_1 (.in(or_1_out));

  // Notes on the sheet:
  //   Prime Number
endmodule
