// Logisim project As2_2.1.circ as structural Verilog: 1 circuit, main circuit main
module main (
  input  A,
  input  B,
  input  C,
  input  D
);

  wire A_nBCD_out, AB_nCD_out, ABC_nD_out, ABCD_out, nABCD_out, not_1_out, not_2_out, not_3_out, not_4_out,
       OR_out;

  not not_1 (not_1_out, A);
  not not_2 (not_2_out, B);
  not not_3 (not_3_out, C);
  not not_4 (not_4_out, D);
  and nABCD (nABCD_out, not_1_out, B, C, D);
  and A_nBCD (A_nBCD_out, A, not_2_out, C, D);
  and AB_nCD (AB_nCD_out, A, B, not_3_out, D);
  and ABC_nD (ABC_nD_out, A, B, C, not_4_out);
  and ABCD (ABCD_out, A, B, C, D);
  or OR (OR_out, nABCD_out, A_nBCD_out, AB_nCD_out, ABC_nD_out, ABCD_out);
  LED led_1 (.in(OR_out));

  // Notes on the sheet:
  //   Majority of bits are 1
endmodule
