// Logisim project As2_2.2.circ as structural Verilog: 1 circuit, main circuit main
module main (
  input  A,
  input  B,
  input  C,
  input  D
);

  wire ABC_out, ABD_out, ACD_out, BCD_out, or_1_out;

  and ABC (ABC_out, A, B, C);
  and ABD (ABD_out, A, B, D);
  and BCD (BCD_out, B, C, D);
  and ACD (ACD_out, A, C, D);
  or or_1 (or_1_out, ABC_out, ABD_out, BCD_out, ACD_out);
  LED led_1 (.in(or_1_out));

  // Notes on the sheet:
  //   Are the majority of bits 1?
endmodule
